// Logisim project CPU.circ as structural Verilog: 1 circuit, main circuit CPU
module CPU (
);

  wire clock_1_out, decoder_1_out0, decoder_1_out1, decoder_1_out2, decoder_1_out3, or_1_out;
  wire [3:0] rom_1_data, rom_1_data_2, rom_1_data_3;
  wire [6:0] bit_extender_2_out;
  wire [15:0] main_1_p1, main_1_p6, main_1_p7;
  wire [23:0] adder_1_out, bit_extender_1_out, multiplexer_1_out, register_1_q;
  wire [23:20] rom_1_data_4;
  wire [31:0] register_2_q, register_3_q;

  Multiplexer #(.width(24), .enable("false")) multiplexer_1 (
    .in0({rom_1_data_4, rom_1_data_3, rom_1_data_2, rom_1_data, rom_1_data_4, rom_1_data_3}),
    .in1(adder_1_out), .out(multiplexer_1_out), .sel(decoder_1_out3));
  assign bit_extender_1_out = {{23{1'b0}}, 1'b1};  // Bit_Extender bit_extender_1
  Register #(.width(24)) register_1 (.D(multiplexer_1_out), .Q(register_1_q));  // open: en, clk, clr
  Adder #(.width(24)) adder_1 (.a(register_1_q), .b(bit_extender_1_out), .out(adder_1_out));  // open: cin, cout
  ROM #(.addrWidth(24), .dataWidth(32)) rom_1 (
    .addr(register_1_q),
    .data({rom_1_data_4, rom_1_data_3, rom_1_data_2, rom_1_data, rom_1_data_4, rom_1_data_3, rom_1_data_2, rom_1_data}));  // open: sel
  Decoder #(.select(4), .enable("false")) decoder_1 (
    .out0(decoder_1_out0), .out1(decoder_1_out1), .out2(decoder_1_out2), .out3(decoder_1_out3),
    .sel(rom_1_data));  // open: out4, out5, out6, out7, out8, out9, out10, out11, out12, out13, out14, out15
  or or_1 (or_1_out, decoder_1_out1, decoder_1_out2, decoder_1_out0);
  Clock clock_1 (.out(clock_1_out));
  ALU alu_1 (.A(main_1_p6), .B(main_1_p1), .Enable(decoder_1_out2));  // open: INSTR, OUT
  // REGARRAY_main main_1: pin names not known; wires that end beside it: main_1_p1, rom_1_data_4, rom_1_data_4, or_1_out, clock_1_out, main_1_p6, main_1_p7
  Multiplexer #(.select(2), .width(16)) multiplexer_2 (
    .in0(main_1_p7), .in1({rom_1_data_4, rom_1_data_3, rom_1_data_2, rom_1_data}), .out(main_1_p1));  // open: in2, in3, sel, en
  Register #(.width(32)) register_2 (.Q(register_2_q), .clk(clock_1_out));  // open: D, en, clr
  Register #(.width(32)) register_3 (.Q(register_3_q), .clk(clock_1_out));  // open: D, en, clr
  RAM #(.dataWidth(16)) ram_1 (.addr({rom_1_data_4, rom_1_data_3}), .clk(clock_1_out));  // open: data, sel, ld, clr
  Bit_Extender #(.out_width(7)) bit_extender_2 (.in(main_1_p1[15:8]), .out(bit_extender_2_out));
  DotMatrix #(.matrixcols(8), .matrixrows(8)) dotmatrix_1 (
    .col0(register_2_q[31:24]), .col1(register_2_q[23:16]), .col2(register_2_q[15:8]),
    .col3(register_2_q[7:0]), .col4(register_3_q[31:24]), .col5(register_3_q[23:16]),
    .col6(register_3_q[15:8]), .col7(register_3_q[7:0]));
  TTY tty_1 (.data(bit_extender_2_out), .clk(clock_1_out));  // open: we, clr

  // Notes on the sheet:
  //   0=immediate
  //   1=mov
  //   2=calc
  //   3=jmp
  //   Write
  //   Read
endmodule
